# Fritzing sketch Montaje.DHT11.y.Raspberry (saved by Fritzing 0.9.2b)
breadboards: 1

parts:
  DHT1 = DHT11 Humitidy and Temperature Sensor
  Raspberry_Pi1 = Raspberry Pi 2
  R1 = Resistor [tolerance=±5% resistance=10 package=THT]

nets:
  VDD: DHT1.VDD, Raspberry_Pi1.3v3, R1.Pin_0
  N1: DHT1.DATA, Raspberry_Pi1.GPIO4, R1.Pin_1
  GND: DHT1.GND, Raspberry_Pi1.GND

custom parts:
  DHT11 Humitidy and Temperature Sensor: DHT11 Humidity and Temperature Sensor
